# Fritzing sketch schema (saved by Fritzing 0.8.7b)

parts:
  Arduino_Nano_3_0 = Arduino Nano (Rev3.0)
  HMC5883L_3_Axis_Magnetometer = Triple Axis Magnetometer - HMC5883 Breakout

nets:
  GND: Arduino_Nano_3_0.GND, HMC5883L_3_Axis_Magnetometer.GND
  5V: Arduino_Nano_3_0.5V, HMC5883L_3_Axis_Magnetometer.VCC
  N1: Arduino_Nano_3_0.A5, HMC5883L_3_Axis_Magnetometer.SDA
  N2: Arduino_Nano_3_0.A4, HMC5883L_3_Axis_Magnetometer.SCL
